# Fritzing sketch goawsv2 (saved by Fritzing 0.9.10b)
circuit board: 12.7458cm x 9.58073cm
breadboards: 3

parts:
  Mod1 = Raspberry Pi Pico
  C1 = Ceramic Capacitor [capacitance=12pF voltage=35V package="100 mil [THT, multilayer]"]
  R1 = Resistor [tolerance=±5% power=0.25 resistance=1k package=THT]
  Rain = male pin header, 2 pins [form="♂ (male)"]
  switch = male pin header, 2 pins [form="♂ (male)"]
  R2 = Resistor [tolerance=±5% power=0.25 resistance=1k package=THT]
  Wind = male pin header, 4 pins [form="♂ (male)"]
  Q1 = NPN-Transistor [package="TO92 [THT]"]
  C2 = Ceramic Capacitor [capacitance=12pF voltage=35V package="100 mil [THT, multilayer]"]
  sensor = male pin header, 6 pins [form="♂ (male)"]
  R3 = Resistor [tolerance=±5% power=0.25 resistance=10k package=THT]
  rak811 = XBEE-1 [package=xbee-1]
  R4 = Resistor [tolerance=±5% power=0.25 resistance=100k package=THT]
  R5 = Resistor [tolerance=±5% power=0.25 resistance=100k package=THT]
  LEDs = male pin header, 6 pins [form="♂ (male)"]
  R6 = Resistor [tolerance=±5% power=0.25 resistance=220 package=THT]
  R7 = Resistor [tolerance=±5% power=0.25 resistance=220 package=THT]
  R8 = Resistor [tolerance=±5% power=0.25 resistance=220 package=THT]
  D1 = Schottky Diode [part_number=1N5817 package="300 mil [THT]"]
  BQ24074 = Adafruit BQ24074 Solar-DC-USB Lipo Charger

nets:
  N1: Mod1.pin_1, rak811.DIN
  N2: Mod1.pin_2, rak811.DOUT
  GND: Mod1.pin_3, Mod1.pin_13, Mod1.pin_18, Mod1.pin_23, Mod1.pin_28, Mod1.pin_38, C1.0, Rain.pin2, Wind.pin3, Wind.pin4, Q1.E, C2.0, sensor.pin4, rak811.GND, R5.Pin_0, LEDs.pin1, LEDs.pin3, LEDs.pin5, BQ24074.GND
  N3: Mod1.pin_4, R2.Pin_1
  N4: Mod1.pin_5, R1.Pin_1
  N5: Mod1.pin_17, R8.Pin_1
  N6: Mod1.pin_19, R7.Pin_1
  N7: Mod1.pin_20, R6.Pin_1
  N8: Mod1.pin_21, sensor.pin6
  N9: Mod1.pin_22, sensor.pin5
  N10: Mod1.pin_24, sensor.pin3
  N11: Mod1.pin_25, sensor.pin2
  N12: Mod1.pin_29, Q1.B
  N13: Mod1.pin_30, Q1.C
  N14: Mod1.pin_31, Wind.pin1, R3.Pin_0
  N15: Mod1.pin_32, R4.Pin_0, R5.Pin_1
  N16: Mod1.pin_36, sensor.pin1, R3.Pin_1, rak811.VDD
  N17: Mod1.pin_39, D1.cathode
  N18: C1.1, R1.Pin_0, Rain.pin1
  N19: switch.pin1, BQ24074.OUT
  N20: switch.pin2, D1.anode
  N21: R2.Pin_0, Wind.pin2, C2.1
  N22: R4.Pin_1, BQ24074.VLIPO
  N23: LEDs.pin2, R6.Pin_0
  N24: LEDs.pin4, R7.Pin_0
  N25: LEDs.pin6, R8.Pin_0

notes:
  openaws v1.0.0
  pico + ds3231

custom parts:
  Raspberry Pi Pico: Raspberry Pi Pico. Based around the RP2040 microcontroller the Pico is a low cost microcontroller device bringing Raspberry Pi quality, cost, and easy of use to the microcontroller space. Jan 2021, Split part in to two versions: tht (this one) and SMD. This one will drill holes for a .1 in header in pcb to allow plugging in the module as well as providing pads to solder the module to the top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
